# Fritzing sketch Sample Circuit (saved by Fritzing 0.9.4)
breadboards: 1

parts:
  LED1 = LED - 5mm [color="Red (633nm)" package="5 mm [THT]"]
  VCC1 = Battery
  R1 = Resistor [tolerance=±5% resistance=220 package=THT]

nets:
  N1: LED1.cathode, VCC1.-
  N2: LED1.anode, R1.Pin_0
  N3: VCC1.+, R1.Pin_1
