# Fritzing sketch hex inverter (saved by Fritzing 0.9.4)
breadboards: 1

parts:
  U1 = 74HC04_HEX_INVERTER [package=dil14]

nets:
  GND: U1.1A
  N1: U1.1Y, U1.2A
  N2: U1.2Y, U1.3A
  N3: U1.3Y, U1.4A
  N4: U1.4Y, U1.5A
  N5: U1.5Y, U1.6A
