// Logisim project Adder_Subtractor.circ as structural Verilog: 1 circuit, main circuit main
module main (
  input  Cin,
  input  a1,
  input  b1,
  input  a2,
  input  b2,
  input  a3,
  input  b3,
  input  a4,
  input  b4,
  output s1,
  output s2,
  output s3,
  output s4,
  output Cout
);

  wire adder_1_cout, adder_2_cout, adder_3_cout, xor_1_out, xor_2_out, xor_3_out, xor_4_out;

  xor xor_1 (xor_1_out, Cin, b1);
  xor xor_2 (xor_2_out, Cin, b2);
  xor xor_3 (xor_3_out, Cin, b3);
  xor xor_4 (xor_4_out, Cin, b4);
  Adder #(.width(1)) adder_1 (.a(a1), .b(xor_1_out), .out(s1), .cin(Cin), .cout(adder_1_cout));
  Adder #(.width(1)) adder_2 (.a(a2), .b(xor_2_out), .out(s2), .cin(adder_1_cout), .cout(adder_2_cout));
  Adder #(.width(1)) adder_3 (.a(a3), .b(xor_3_out), .out(s3), .cin(adder_2_cout), .cout(adder_3_cout));
  Adder #(.width(1)) adder_4 (.a(a4), .b(xor_4_out), .out(s4), .cin(adder_3_cout), .cout(Cout));
  // XOR_Gate xor_5 has open pins: in0=adder_3_cout, in3=Cout, out=open
endmodule
